# Fritzing sketch TCA9548A-multiplexer (saved by Fritzing 0.9.3b)
breadboards: 1

parts:
  Part1 = Adafruit TCA9548A
  Part2 = Adafruit VL53L0X Time of Flight Distance Sensor [part_number="Adafruit #3317"]
  Part3 = Adafruit VL53L0X Time of Flight Distance Sensor [part_number="Adafruit #3317"]
  Part4 = Adafruit Feather M0 Express [part_number="Adafruit #3403"]

nets:
  N1: Part1.7SDA, Part2.SDA
  N2: Part1.7SCL, Part2.SCL
  VIN: Part1.VCC, Part2.VIN, Part3.VIN, Part4.+3V3
  GND: Part1.GND, Part2.2.8V, Part3.GND, Part4.GND
  N3: Part1.0SDA, Part3.SDA
  N4: Part1.0SCL, Part3.SCL
  N5: Part1.1SDA, Part4.SDA
  N6: Part1.1SCL, Part4.SCL

notes:
  The sensors are connected to channels 0 and 7, not 0 and 1 as in the code.

custom parts:
  Adafruit TCA9548A: You just found the perfect I2C sensor, and you want to wire up two or three or more of them to your Arduino when you realize "Uh oh, this chip has a fixed I2C address, and from what I know about I2C, you cannot have two devices with the same address on the same SDA/SCL pins!" Are you out of luck? You would be, if you didn't have this ultra-cool TCA9548A 1-to-8 I2C multiplexer! Finally, a way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
  Adafruit VL53L0X Time of Flight Distance Sensor: The VL53L0X is a Time of Flight distance sensor like no other you've used! The sensor contains a very tiny invisible laser source, and a matching sensor. The VL53L0X can detect the "time of flight", or how long the light has taken to bounce back to the sensor. Since it uses a very narrow light source, it is good for determining distance of only the surface directly in front of it. Unlike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
  Adafruit Feather M0 Express: We love all our Feathers equally, but this Feather is very special. It's our first Feather that is specifically designed for use with CircuitPython! CircuitPython is our beginner-oriented flavor of MicroPython - and as the name hints at, its a small but full-featured version of the popular Python programming language specifically for use with circuitry and electronics. That doesn't mean you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
